# Fritzing sketch PP2PS2 (saved by Fritzing 0.9.3b)
breadboards: 1

parts:
  パーツ1 = Arduino Nano (Rev3.0)
  IC1 = IC, DIP package, 14 pins [chip_label=74HC125]
  J1 = shrouded pin header, 16 pins [form="♂ (shrouded male)"]
  J1_2 = Camdenboss CTB0158-9 [part_number=CTB0158-9 package=THT]

nets:
  N1: パーツ1.GND, IC1.pin2, IC1.pin5, IC1.pin7, J1.pin4, J1_2.pin4
  N2: パーツ1.D2, J1.pin2
  N3: パーツ1.D4, J1.pin7
  N4: パーツ1.D5, J1.pin3
  N5: パーツ1.D9, IC1.pin1
  N6: パーツ1.D10, J1_2.pin6
  N7: パーツ1.D11/MOSI, J1_2.pin2
  N8: パーツ1.D12/MISO, IC1.pin4
  N9: パーツ1.5V, IC1.pin14, J1.pin1
  N10: パーツ1.D13/SCK, J1_2.pin7
  N11: IC1.pin3, J1_2.pin9
  N12: IC1.pin6, J1_2.pin1
  N13: IC1.pin9, IC1.pin10, IC1.pin12, IC1.pin13

notes:
  X1: Precision Pro DB15 Connector
  1. Vcc (5V) -> 5V
  2. SCK -> D2
  3. Trigger -> D5
  4. GND -> GND
  5. NC
  6. NC
  7. Data (MOSI) -> D4
  8. NC
  9. NC
  10. NC
  11. NC
  12. NC
  13. NC
  14. NC
  15. NC
  Arduino 接続ピン
  D2 - X1 2: PP SCK
  D3 - NC
  D4 - X1 7: PP Data
  D5 - X1 3: PP Trigger
  D6 -
  D7 -
  D8 -
  D9 - IC1 1
  D10 - J1 6: PS2 Attension
  D11 - J1 2: PS2 Command
  D12 - IC1 4
  D13 - J1 7: PS2 Clock
  J1: PlayStation2 Controller
  1. Data -> IC1 6
  2. Command -> D11
  3. Motor Power (7-9V) -> NC
  4. GND -> GND
  5. Vcc (3.3V) -> NC
  6. Attension -> D10
  7. Clock -> D13
  8. Unknown
  9. Acknoledge -> IC1 3
